// Logisim project problem1.circ as structural Verilog: 4 circuits, main circuit 1a
module _1a (
  input  A,
  input  B,
  input  C
);

  wire and_1_out, and_2_out, and_3_out, and_4_out, or_1_out;

  and and_1 (and_1_out, A, B);
  and and_2 (and_2_out, B, C);
  and and_3 (and_3_out, A, C);
  and and_4 (and_4_out, A, B, C);
  or or_1 (or_1_out, and_1_out, and_4_out, and_3_out, and_2_out);
  LED led_1 (.in(or_1_out));
endmodule

module _1b (
  input  A,
  input  B,
  input  C
);

  wire and_1_out, and_2_out, and_3_out, not_1_out, not_2_out, not_3_out, or_1_out;

  not not_1 (not_1_out, A);
  not not_2 (not_2_out, B);
  not not_3 (not_3_out, C);
  and and_1 (and_1_out, not_1_out, not_2_out);
  and and_2 (and_2_out, not_1_out, B, not_3_out);
  and and_3 (and_3_out, not_2_out, A, not_3_out);
  or or_1 (or_1_out, and_1_out, and_2_out, and_3_out);
  LED led_1 (.in(or_1_out));
endmodule

module _1ai (
  input  A,
  input  B,
  input  C
);

  wire ic_7408_1_p4, ic_7408_2_p3, ic_7408_3_p3, ic_7411_1_p3, ic_7432_1_p3, ic_7432_2_p3, ic_7432_3_p3;

  // IC_7411 ic_7411_1: pin names not known; wires that end beside it: A, B, ic_7411_1_p3
  // IC_7408 ic_7408_1: pin names not known; wires that end beside it: A, C, C, ic_7408_1_p4
  // IC_7408 ic_7408_2: pin names not known; wires that end beside it: B, C, ic_7408_2_p3
  // IC_7408 ic_7408_3: pin names not known; wires that end beside it: B, A, ic_7408_3_p3
  // IC_7432 ic_7432_1: pin names not known; wires that end beside it: ic_7408_3_p3, ic_7411_1_p3, ic_7432_1_p3
  // IC_7432 ic_7432_2: pin names not known; wires that end beside it: ic_7408_2_p3, ic_7408_1_p4, ic_7432_2_p3
  // IC_7432 ic_7432_3: pin names not known; wires that end beside it: ic_7432_1_p3, ic_7432_2_p3, ic_7432_3_p3
  LED led_1 (.in(ic_7432_3_p3));
endmodule

module _1bi (
  input  A,
  input  B,
  input  C
);

  wire ic_7404_1_p4, ic_7404_1_p5, ic_7404_1_p6, ic_7408_1_p4, ic_7411_1_p3, ic_7411_2_p4, ic_7432_1_p3,
       ic_7432_2_p3;

  // IC_7404 ic_7404_1: pin names not known; wires that end beside it: A, B, C, ic_7404_1_p4, ic_7404_1_p5, ic_7404_1_p6
  // IC_7411 ic_7411_1: pin names not known; wires that end beside it: ic_7404_1_p4, B, ic_7411_1_p3
  // IC_7408 ic_7408_1: pin names not known; wires that end beside it: ic_7404_1_p6, ic_7404_1_p4, ic_7404_1_p5, ic_7408_1_p4
  // IC_7411 ic_7411_2: pin names not known; wires that end beside it: A, ic_7404_1_p5, ic_7404_1_p6, ic_7411_2_p4
  // IC_7432 ic_7432_1: pin names not known; wires that end beside it: ic_7411_1_p3, ic_7408_1_p4, ic_7432_1_p3
  // IC_7432 ic_7432_2: pin names not known; wires that end beside it: ic_7432_1_p3, ic_7411_2_p4, ic_7432_2_p3
  LED led_1 (.in(ic_7432_2_p3));
endmodule
