// Logisim project problem2.circ as structural Verilog: 1 circuit, main circuit main
module main (
  input  Car0,
  input  Car1,
  input  Car2,
  input  Car3,
  input  Car4,
  input  Car5,
  input  Car6
);

  wire A_out, B_out, C_out, Car0Dec_out, Car1Dec_out, Car2Dec_out, Car3Dec_out, Car4Dec_out, Car5Dec_out,
       Car6Dec_out, not_1_out, not_2_out, not_3_out, SegA_out, SegB_out, SegC_out, SegD_out, SegE_out,
       SegF_out, SegG_out;

  or C (C_out, Car0, Car1, Car3, Car5);
  or B (B_out, Car2, Car0, Car3, Car6);
  or A (A_out, Car4, Car5, Car0, Car6);
  or SegA (SegA_out, Car0Dec_out, Car5Dec_out, Car3Dec_out, Car6Dec_out, Car2Dec_out);
  and Car0Dec (Car0Dec_out, C_out, B_out, A_out);
  not not_1 (not_1_out, C_out);
  not not_2 (not_2_out, B_out);
  not not_3 (not_3_out, A_out);
  or SegB (SegB_out, Car0Dec_out, Car2Dec_out, Car3Dec_out, Car4Dec_out, Car1Dec_out);
  and Car1Dec (Car1Dec_out, C_out, not_2_out, not_3_out);
  _7_Segment_Display u_7_segment_display_1 (
    .g(SegG_out), .f(SegF_out), .a(SegA_out), .b(SegB_out), .e(SegE_out), .d(SegD_out), .c(SegC_out));  // open: dp
  or SegC (SegC_out, Car6Dec_out, Car0Dec_out, Car3Dec_out, Car5Dec_out, Car1Dec_out, Car4Dec_out);
  and Car2Dec (Car2Dec_out, not_1_out, B_out, not_3_out);
  or SegD (SegD_out, Car0Dec_out, Car3Dec_out, Car5Dec_out, Car6Dec_out, Car2Dec_out);
  and Car3Dec (Car3Dec_out, C_out, B_out, not_3_out);
  or SegE (SegE_out, Car0Dec_out, Car6Dec_out, Car2Dec_out);
  and Car4Dec (Car4Dec_out, not_1_out, not_2_out, A_out);
  or SegF (SegF_out, Car0Dec_out, Car5Dec_out, Car6Dec_out, Car4Dec_out);
  and Car5Dec (Car5Dec_out, C_out, not_2_out, A_out);
  or SegG (SegG_out, Car2Dec_out, Car5Dec_out, Car3Dec_out, Car6Dec_out, Car4Dec_out);
  and Car6Dec (Car6Dec_out, not_1_out, B_out, A_out);
endmodule
