// Logisim project problem1.circ as structural Verilog: 1 circuit, main circuit main
module main (
  input  in_1
);

  wire clock_1_out, nand_1_out, nand_2_out, nand_3_out, nand_4_out, nand_5_out, nand_6_out, nand_7_out,
       nand_8_out, nand_9_out, nand_10_out, nand_11_out;

  Clock clock_1 (.out(clock_1_out));
  nand nand_1 (nand_1_out, in_1, in_1);
  nand nand_2 (nand_2_out, clock_1_out, clock_1_out);
  nand nand_3 (nand_3_out, in_1, nand_2_out);
  nand nand_4 (nand_4_out, nand_2_out, nand_1_out);
  nand nand_5 (nand_5_out, nand_3_out, nand_6_out);
  nand nand_6 (nand_6_out, nand_5_out, nand_4_out);
  nand nand_7 (nand_7_out, nand_5_out, nand_5_out);
  nand nand_8 (nand_8_out, nand_5_out, clock_1_out);
  nand nand_9 (nand_9_out, clock_1_out, nand_7_out);
  nand nand_10 (nand_10_out, nand_8_out, nand_11_out);
  nand nand_11 (nand_11_out, nand_10_out, nand_9_out);

  // Notes on the sheet:
  //   Master
  //   Servant
endmodule
