// Logisim project problem2.circ as structural Verilog: 1 circuit, main circuit main
module main (
);

  wire and_1_out, button_1_out, button_2_out, clock_1_out, d_ff_1_q, d_ff_1_qn, nand_1_out, nand_2_out,
       nand_3_out, nand_4_out, nand_5_out, nand_6_out, nand_7_out, nand_8_out, nor_1_out, not_1_out,
       not_2_out, undriven;

  LED ButtonLED (.in(button_1_out));
  Button button_1 (.out(button_1_out));
  Clock clock_1 (.out(clock_1_out));
  not not_1 (not_1_out, nand_8_out);
  not not_2 (not_2_out, undriven);
  nor nor_1 (nor_1_out, nand_7_out, clock_1_out);
  and and_1 (and_1_out, clock_1_out, not_1_out);
  nand nand_1 (nand_1_out, undriven, clock_1_out);
  nand nand_2 (nand_2_out, clock_1_out, not_2_out);
  nand nand_3 (nand_3_out, button_1_out, nor_1_out);
  nand nand_4 (nand_4_out, and_1_out, button_1_out);
  nand nand_5 (nand_5_out, nand_1_out, nand_6_out);
  nand nand_6 (nand_6_out, nand_5_out, nand_2_out);
  nand nand_7 (nand_7_out, nand_3_out, nand_8_out);
  nand nand_8 (nand_8_out, nand_7_out, nand_4_out);
  LED ACLED (.in(nand_5_out));
  Button button_2 (.out(button_2_out));
  D_Flip_Flop d_ff_1 (.D(d_ff_1_qn), .clk(button_2_out), .Q(d_ff_1_q), .Qn(d_ff_1_qn));  // open: preset, reset
  LED led_1 (.in(d_ff_1_q));

  // Notes on the sheet:
  //   7436
  //   7408
  //   7404
  //   7400
  //   7474
endmodule
