// Logisim project problem3.circ as structural Verilog: 1 circuit, main circuit main
module main (
  input  A0,
  input  A1,
  input  A2,
  input  A3
);

  wire AC_out, and_1_out, button_1_out, clock_1_out, Door1_out, Door2_out, Door3_out, Door4_out, Engine_out,
       nand_1_out, nand_2_out, nand_3_out, nand_4_out, nand_5_out, nand_6_out, nand_7_out, nand_8_out,
       nand_9_out, nand_10_out, nand_11_out, nand_12_out, nand_13_out, nand_14_out, nand_15_out, nand_16_out,
       nand_17_out, nand_18_out, nand_19_out, nand_20_out, nand_21_out, nand_22_out, nand_23_out,
       nand_24_out, nand_25_out, nand_26_out, nand_27_out, nand_28_out, nand_29_out, nand_30_out,
       nand_31_out, nand_32_out, nand_33_out, nand_34_out, nand_35_out, nand_36_out, nand_37_out,
       nand_38_out, nand_39_out, nand_40_out, nand_41_out, nand_42_out, nand_43_out, nand_44_out,
       nand_45_out, nand_46_out, nand_47_out, nand_48_out, nand_49_out, nand_50_out, nand_51_out,
       nand_52_out, nand_53_out, nand_54_out, nand_55_out, nand_56_out, nand_57_out, nand_58_out,
       nand_59_out, nand_60_out, nand_61_out, nand_62_out, nand_63_out, nand_64_out, nor_1_out, not_1_out,
       not_2_out, not_3_out, not_4_out, not_5_out, not_6_out, not_7_out, not_8_out, not_9_out, not_10_out,
       not_11_out, not_12_out, not_13_out, not_14_out, not_15_out, not_16_out, Wipers_out;

  Button button_1 (.out(button_1_out));
  and AC (AC_out, A3, ~A2, ~A1, ~A0);  // AND_Gate
  and Door1 (Door1_out, A3, ~A2, ~A1, A0);  // AND_Gate
  and Door2 (Door2_out, ~A3, ~A2, A1, ~A0);  // AND_Gate
  and Door3 (Door3_out, A3, ~A2, A1, A0);  // AND_Gate
  and Door4 (Door4_out, ~A3, A2, ~A1, ~A0);  // AND_Gate
  and Engine (Engine_out, A3, A2, ~A1, A0);  // AND_Gate
  and Wipers (Wipers_out, ~A3, A2, A1, ~A0);  // AND_Gate
  not not_1 (not_1_out, Wipers_out);
  not not_2 (not_2_out, Engine_out);
  not not_3 (not_3_out, Door4_out);
  not not_4 (not_4_out, Door3_out);
  not not_5 (not_5_out, Door2_out);
  not not_6 (not_6_out, Door1_out);
  not not_7 (not_7_out, AC_out);
  Clock clock_1 (.out(clock_1_out));
  nand nand_1 (nand_1_out, Wipers_out, clock_1_out);
  nand nand_2 (nand_2_out, clock_1_out, not_1_out);
  nand nand_3 (nand_3_out, Engine_out, clock_1_out);
  nand nand_4 (nand_4_out, clock_1_out, not_2_out);
  nand nand_5 (nand_5_out, Door4_out, clock_1_out);
  nand nand_6 (nand_6_out, clock_1_out, not_3_out);
  nand nand_7 (nand_7_out, Door3_out, clock_1_out);
  nand nand_8 (nand_8_out, clock_1_out, not_4_out);
  nand nand_9 (nand_9_out, Door2_out, clock_1_out);
  nand nand_10 (nand_10_out, clock_1_out, not_5_out);
  nand nand_11 (nand_11_out, Door1_out, clock_1_out);
  nand nand_12 (nand_12_out, clock_1_out, not_6_out);
  nand nand_13 (nand_13_out, AC_out, clock_1_out);
  nand nand_14 (nand_14_out, clock_1_out, not_7_out);
  nor nor_1 (nor_1_out, nand_31_out, clock_1_out);
  not not_8 (not_8_out, nand_32_out);
  nand nand_15 (nand_15_out, nand_1_out, nand_16_out);
  nand nand_16 (nand_16_out, nand_15_out, nand_2_out);
  nand nand_17 (nand_17_out, nand_3_out, nand_18_out);
  nand nand_18 (nand_18_out, nand_17_out, nand_4_out);
  nand nand_19 (nand_19_out, nand_5_out, nand_20_out);
  nand nand_20 (nand_20_out, nand_19_out, nand_6_out);
  nand nand_21 (nand_21_out, nand_7_out, nand_22_out);
  nand nand_22 (nand_22_out, nand_21_out, nand_8_out);
  nand nand_23 (nand_23_out, nand_9_out, nand_24_out);
  nand nand_24 (nand_24_out, nand_23_out, nand_10_out);
  nand nand_25 (nand_25_out, nand_11_out, nand_26_out);
  nand nand_26 (nand_26_out, nand_25_out, nand_12_out);
  nand nand_27 (nand_27_out, nand_13_out, nand_28_out);
  nand nand_28 (nand_28_out, nand_27_out, nand_14_out);
  and and_1 (and_1_out, clock_1_out, not_8_out);
  nand nand_29 (nand_29_out, button_1_out, nor_1_out);
  nand nand_30 (nand_30_out, and_1_out, button_1_out);
  nand nand_31 (nand_31_out, nand_29_out, nand_32_out);
  nand nand_32 (nand_32_out, nand_31_out, nand_30_out);
  not not_9 (not_9_out, nand_31_out);
  nand nand_33 (nand_33_out, nand_31_out, clock_1_out);
  nand nand_34 (nand_34_out, clock_1_out, not_9_out);
  nand nand_35 (nand_35_out, nand_33_out, nand_36_out);
  nand nand_36 (nand_36_out, nand_35_out, nand_34_out);
  not not_10 (not_10_out, nand_15_out);
  not not_11 (not_11_out, nand_17_out);
  not not_12 (not_12_out, nand_19_out);
  not not_13 (not_13_out, nand_21_out);
  not not_14 (not_14_out, nand_23_out);
  not not_15 (not_15_out, nand_25_out);
  not not_16 (not_16_out, nand_27_out);
  nand nand_37 (nand_37_out, nand_15_out, nand_35_out);
  nand nand_38 (nand_38_out, nand_35_out, not_10_out);
  nand nand_39 (nand_39_out, nand_17_out, nand_35_out);
  nand nand_40 (nand_40_out, nand_35_out, not_11_out);
  nand nand_41 (nand_41_out, nand_19_out, nand_35_out);
  nand nand_42 (nand_42_out, nand_35_out, not_12_out);
  nand nand_43 (nand_43_out, nand_21_out, nand_35_out);
  nand nand_44 (nand_44_out, nand_35_out, not_13_out);
  nand nand_45 (nand_45_out, nand_23_out, nand_35_out);
  nand nand_46 (nand_46_out, nand_35_out, not_14_out);
  nand nand_47 (nand_47_out, nand_25_out, nand_35_out);
  nand nand_48 (nand_48_out, nand_35_out, not_15_out);
  nand nand_49 (nand_49_out, nand_27_out, nand_35_out);
  nand nand_50 (nand_50_out, nand_35_out, not_16_out);
  nand nand_51 (nand_51_out, nand_37_out, nand_52_out);
  nand nand_52 (nand_52_out, nand_51_out, nand_38_out);
  nand nand_53 (nand_53_out, nand_39_out, nand_54_out);
  nand nand_54 (nand_54_out, nand_53_out, nand_40_out);
  nand nand_55 (nand_55_out, nand_41_out, nand_56_out);
  nand nand_56 (nand_56_out, nand_55_out, nand_42_out);
  nand nand_57 (nand_57_out, nand_43_out, nand_58_out);
  nand nand_58 (nand_58_out, nand_57_out, nand_44_out);
  nand nand_59 (nand_59_out, nand_45_out, nand_60_out);
  nand nand_60 (nand_60_out, nand_59_out, nand_46_out);
  nand nand_61 (nand_61_out, nand_47_out, nand_62_out);
  nand nand_62 (nand_62_out, nand_61_out, nand_48_out);
  nand nand_63 (nand_63_out, nand_49_out, nand_64_out);
  nand nand_64 (nand_64_out, nand_63_out, nand_50_out);
  LED WiperLED (.in(nand_51_out));
  LED EngineLED (.in(nand_53_out));
  LED Door4LED (.in(nand_55_out));
  LED Door3LED (.in(nand_57_out));
  LED Door2LED (.in(nand_59_out));
  LED Door1LED (.in(nand_61_out));
  LED ACLED (.in(nand_63_out));
endmodule
