// Logisim project Problem2Adder.circ as structural Verilog: 6 circuits, main circuit EightBitAdder
module EightBitAdder (
  input  [7:0] A,
  input  [7:0] B,
  input  CarryIn,
  output Overflow,
  output Bit8,
  output Bit7,
  output Bit6,
  output Bit5,
  output Bit4,
  output Bit3,
  output Bit2,
  output Bit1
);

  wire fulladder_2_cout, fulladder_3_cout, fulladder_4_cout, fulladder_5_cout, fulladder_6_cout,
       fulladder_7_cout, fulladder_8_cout;

  FullAdder fulladder_1 (.A(A[7]), .B(B[7]), .Cin(fulladder_2_cout), .Cout(Overflow), .Sum(Bit8));
  FullAdder fulladder_2 (.A(A[6]), .B(B[6]), .Cin(fulladder_3_cout), .Cout(fulladder_2_cout), .Sum(Bit7));
  FullAdder fulladder_3 (.A(A[5]), .B(B[5]), .Cin(fulladder_4_cout), .Cout(fulladder_3_cout), .Sum(Bit6));
  FullAdder fulladder_4 (.A(A[4]), .B(B[4]), .Cin(fulladder_5_cout), .Cout(fulladder_4_cout), .Sum(Bit5));
  FullAdder fulladder_5 (.A(A[3]), .B(B[3]), .Cin(fulladder_6_cout), .Cout(fulladder_5_cout), .Sum(Bit4));
  FullAdder fulladder_6 (.A(A[2]), .B(B[2]), .Cin(fulladder_7_cout), .Cout(fulladder_6_cout), .Sum(Bit3));
  FullAdder fulladder_7 (.A(A[1]), .B(B[1]), .Cin(fulladder_8_cout), .Cout(fulladder_7_cout), .Sum(Bit2));
  FullAdder fulladder_8 (.A(A[0]), .B(B[0]), .Cin(CarryIn), .Cout(fulladder_8_cout), .Sum(Bit1));
endmodule

module HalfAdder (
  input  A,
  input  B,
  output Cout,
  output Sum
);

  and and_1 (Cout, A, B);
  xor xor_1 (Sum, A, B);
endmodule

module FullAdder (
  input  A,
  input  B,
  input  Cin,
  output Cout,
  output Sum
);

  wire halfadder_1_cout, halfadder_1_sum, halfadder_2_cout;

  HalfAdder halfadder_1 (.A(A), .B(B), .Cout(halfadder_1_cout), .Sum(halfadder_1_sum));
  HalfAdder halfadder_2 (.A(halfadder_1_sum), .B(Cin), .Cout(halfadder_2_cout), .Sum(Sum));
  or or_1 (Cout, halfadder_1_cout, halfadder_2_cout);
endmodule

module Inverter (
  input  [7:0] in_1,
  input  [7:0] in_2,
  input  in_3,
  output Sign,
  output [7:0] out_5
);

  wire [7:0] eightbitadder_1_bit1, not_1_out;

  assign not_1_out = ~in_1;  // NOT_Gate not_1, 8 bits wide
  EightBitAdder eightbitadder_1 (
    .A(not_1_out), .B(in_2), .CarryIn(in_3), .Bit8(eightbitadder_1_bit1[7]), .Bit7(eightbitadder_1_bit1[6]),
    .Bit6(eightbitadder_1_bit1[5]), .Bit5(eightbitadder_1_bit1[4]), .Bit4(eightbitadder_1_bit1[3]),
    .Bit3(eightbitadder_1_bit1[2]), .Bit2(eightbitadder_1_bit1[1]), .Bit1(eightbitadder_1_bit1[0]));  // open: Overflow
  Multiplexer #(.width(8)) multiplexer_1 (.in0(in_1), .in1(eightbitadder_1_bit1), .out(out_5), .sel(in_3));

  assign Sign = in_1[7];

  // Notes on the sheet:
  //   not_1 drives only 1 and floats otherwise
endmodule

module Main (
  input  [7:0] in_1,
  input  in_2,
  input  [7:0] in_3,
  input  in_4,
  input  [7:0] in_5,
  input  in_6,
  output [7:0] out_7,
  output [8:0] out_8,
  output [7:0] out_9
);

  wire button_1_out;
  wire [7:0] and_2_out, customswitch_1_out_3, not_1_out, xor_1_out;

  Button button_1 (.out(button_1_out));
  assign out_7 = in_3 & not_1_out;  // AND_Gate and_1, 8 bits wide
  assign not_1_out = ~customswitch_1_out_3;  // NOT_Gate not_1, 8 bits wide
  CustomSwitch customswitch_1 (.in_1(button_1_out), .in_2(in_6), .out_3(customswitch_1_out_3));
  Inverter inverter_1 (.in_1(and_2_out), .in_2(in_5), .in_3(in_4), .out_5(out_9));  // open: Sign
  assign and_2_out = in_3 & customswitch_1_out_3;  // AND_Gate and_2, 8 bits wide
  assign xor_1_out = out_7 ^ out_9;  // XOR_Gate xor_1, 8 bits wide
  EightBitAdder eightbitadder_1 (
    .A(in_1), .B(xor_1_out), .CarryIn(in_2), .Overflow(out_8[8]), .Bit8(out_8[7]), .Bit7(out_8[6]),
    .Bit6(out_8[5]), .Bit5(out_8[4]), .Bit4(out_8[3]), .Bit3(out_8[2]), .Bit2(out_8[1]), .Bit1(out_8[0]));
endmodule

module CustomSwitch (
  input  in_1,
  input  in_2,
  output [7:0] out_3
);

  wire d_ff_1_qn, d_ff_2_qn;
  wire [7:7] d_ff_2_q;

  D_Flip_Flop d_ff_1 (.D(d_ff_2_qn), .clk(in_1), .Qn(d_ff_1_qn));  // open: Q, preset, reset
  D_Flip_Flop d_ff_2 (.D(d_ff_1_qn), .clk(in_1), .Q(d_ff_2_q[7]), .Qn(d_ff_2_qn));  // open: preset, reset
  Demultiplexer #(.width(8)) demultiplexer_1 (.out1(out_3), .in({8{d_ff_2_q[7]}}), .sel(in_2));  // open: out0
endmodule
