// Logisim project Memory.circ as structural Verilog: 6 circuits, main circuit Memory
module Memory (
  input  [3:0] icode,
  input  [63:0] valE,
  input  clk,
  input  [63:0] valA,
  input  [11:0] valP,
  output [63:0] valM
);

  wire memread_1_out_2, memwrite_1_out_2;
  wire [63:0] memadd_1_addrin, memdata_1_datain;

  MemRead memread_1 (.icode(icode), .out_2(memread_1_out_2));
  MemWrite memwrite_1 (.icode(icode), .out_2(memwrite_1_out_2));
  MemAdd memadd_1 (.iCode(icode), .valE(valE), .valA(valA), .AddrIn(memadd_1_addrin));
  MemData memdata_1 (.iCode(icode), .valA(valA), .valP(valP), .DataIn(memdata_1_datain));  // open: in_4
  DataMem datamem_1 (
    .Addr(memadd_1_addrin), .Write(memwrite_1_out_2), .DataIn(memdata_1_datain), .Read(memread_1_out_2),
    .clk(clk), .valM(valM));
endmodule

module MemData (
  input  [3:0] iCode,
  input  [63:0] valA,
  input  [11:0] valP,
  input  [51:0] in_4,
  output [63:0] DataIn
);

  wire comparator_1_eq, comparator_2_eq, comparator_3_eq, comparator_4_eq, comparator_5_eq, or_1_out,
       or_2_out;

  Comparator #(.width(4)) comparator_1 (.a(iCode), .b(4'b1001), .eq(comparator_1_eq));  // open: gt, lt
  Comparator #(.width(4)) comparator_2 (.a(iCode), .b(4'b1010), .eq(comparator_2_eq));  // open: gt, lt
  Comparator #(.width(4)) comparator_3 (.a(iCode), .b(4'b1011), .eq(comparator_3_eq));  // open: gt, lt
  Comparator #(.width(4)) comparator_4 (.a(iCode), .b(4'b1000), .eq(comparator_4_eq));  // open: gt, lt
  Comparator #(.width(4)) comparator_5 (.a(iCode), .b(4'b0100), .eq(comparator_5_eq));  // open: gt, lt
  or or_1 (or_1_out, comparator_5_eq, comparator_1_eq, comparator_2_eq, comparator_3_eq);
  Multiplexer #(.enable("true"), .width(64)) multiplexer_1 (
    .in0(valA), .in1({in_4, valP}), .out(DataIn), .sel(comparator_4_eq), .en(or_2_out));
  or or_2 (or_2_out, or_1_out, comparator_4_eq);
endmodule

module MemAdd (
  input  [3:0] iCode,
  input  [63:0] valE,
  input  [63:0] valA,
  output [63:0] AddrIn
);

  wire comparator_1_eq, comparator_2_eq, comparator_3_eq, comparator_4_eq, comparator_5_eq, comparator_6_eq,
       or_1_out, or_2_out, or_3_out;

  Comparator #(.width(4)) comparator_1 (.a(iCode), .b(4'b0101), .eq(comparator_1_eq));  // open: gt, lt
  Comparator #(.width(4)) comparator_2 (.a(iCode), .b(4'b1000), .eq(comparator_2_eq));  // open: gt, lt
  Comparator #(.width(4)) comparator_3 (.a(iCode), .b(4'b1010), .eq(comparator_3_eq));  // open: gt, lt
  Comparator #(.width(4)) comparator_4 (.a(iCode), .b(4'b1001), .eq(comparator_4_eq));  // open: gt, lt
  Comparator #(.width(4)) comparator_5 (.a(iCode), .b(4'b1011), .eq(comparator_5_eq));  // open: gt, lt
  Comparator #(.width(4)) comparator_6 (.a(iCode), .b(4'b0100), .eq(comparator_6_eq));  // open: gt, lt
  or or_1 (or_1_out, comparator_4_eq, comparator_5_eq);
  or or_2 (or_2_out, comparator_6_eq, comparator_1_eq, comparator_2_eq, comparator_3_eq);
  or or_3 (or_3_out, or_2_out, or_1_out);
  Multiplexer #(.enable("true"), .width(64)) multiplexer_1 (
    .in0(valE), .in1(valA), .out(AddrIn), .sel(or_1_out), .en(or_3_out));
endmodule

module DataMem (
  input  [63:0] Addr,
  input  Write,
  input  [63:0] DataIn,
  input  Read,
  input  clk,
  output [63:0] valM
);

  wire and_1_out, comparator_1_eq, counter_2_q;
  wire [63:0] adder_1_out, counter_1_q, ram_1_dout;

  // Probe on counter_1_q
  Counter #(.max('hffffffffffffffff), .width(64)) counter_1 (
    .up(1'b1), .count(1'b1), .clk(clk), .Q(counter_1_q));  // open: clr, load, D, carry
  Adder #(.width(64)) adder_1 (.a(Addr), .b(counter_1_q), .out(adder_1_out));  // open: cin, cout
  RAM #(.addrWidth(16), .dataWidth(64)) ram_1 (
    .addr(adder_1_out[15:0]), .we(Write), .oe(Read), .clk(clk), .din(DataIn), .dout(ram_1_dout));
  and and_1 (and_1_out, Read, clk);
  Counter #(.max('h1), .ongoal("stay"), .width(1)) counter_2 (
    .count(1'b1), .clk(and_1_out), .Q(counter_2_q));  // open: clr, load, up, D, carry
  Comparator #(.width(1)) comparator_1 (.a(counter_2_q), .b(1'b0), .eq(comparator_1_eq));  // open: gt, lt
  Multiplexer #(.width(64)) multiplexer_1 (.in0(ram_1_dout), .in1({64{1'b0}}), .out(valM), .sel(comparator_1_eq));
endmodule

module MemRead (
  input  [3:0] icode,
  output out_2
);

  wire comparator_1_eq, comparator_2_eq, comparator_3_eq;

  Comparator #(.width(4)) comparator_1 (.a(icode), .b(4'b0100), .eq(comparator_1_eq));  // open: gt, lt
  Comparator #(.width(4)) comparator_2 (.a(icode), .b(4'b1000), .eq(comparator_2_eq));  // open: gt, lt
  Comparator #(.width(4)) comparator_3 (.a(icode), .b(4'b1010), .eq(comparator_3_eq));  // open: gt, lt
  or or_1 (out_2, comparator_1_eq, comparator_2_eq, comparator_3_eq);
endmodule

module MemWrite (
  input  [3:0] icode,
  output out_2
);

  wire comparator_1_eq, comparator_2_eq, comparator_3_eq;

  Comparator #(.width(4)) comparator_1 (.a(icode), .b(4'b0100), .eq(comparator_1_eq));  // open: gt, lt
  Comparator #(.width(4)) comparator_2 (.a(icode), .b(4'b1001), .eq(comparator_2_eq));  // open: gt, lt
  Comparator #(.width(4)) comparator_3 (.a(icode), .b(4'b1011), .eq(comparator_3_eq));  // open: gt, lt
  or or_1 (out_2, comparator_1_eq, comparator_2_eq, comparator_3_eq);
endmodule
