// Logisim project PCStage.circ as structural Verilog: 1 circuit, main circuit main
module main (
  input  [63:0] valM,
  input  [63:0] valP,
  input  [63:0] valC,
  input  cnd,
  input  [3:0] iCode,
  output [63:0] updatedPC
);

  wire clock_1_out;
  wire [63:0] multiplexer_1_out, multiplexer_2_out;

  Multiplexer #(.width(64)) multiplexer_1 (.in0(valP), .in1(valC), .out(multiplexer_1_out), .sel(cnd));
  Multiplexer #(.select(4), .width(64)) multiplexer_2 (
    .in0(valP), .in1(valP), .in2(valP), .in3(valP), .in4(valP), .in5(valP), .in6(valP), .in7(valP),
    .in8(valP), .in9(multiplexer_1_out), .in10(valC), .in11(valM), .in12(valP), .out(multiplexer_2_out),
    .sel(iCode));  // open: in13, in14, in15
  Clock clock_1 (.out(clock_1_out));
  Register #(.width(64)) register_1 (.D(multiplexer_2_out), .clk(clock_1_out), .Q(updatedPC));  // open: en, clr
endmodule
