// Logisim project WriteBack.circ as structural Verilog: 1 circuit, main circuit main
module main (
  input  [3:0] rB,
  input  [3:0] rA,
  input  [3:0] iCode,
  output [3:0] dstE,
  output [3:0] dstM
);

  Multiplexer #(.select(4), .width(4)) multiplexer_1 (
    .in0(4'b1111), .in1(4'b1111), .in2(4'b0100), .in3(rB), .in4(4'b1111), .in5(4'b1111), .in6(rB),
    .in7(4'b1111), .in8(4'b0100), .in9(4'b0100), .in10(4'b0100), .in11(4'b0100), .in12(4'b1111),
    .in13(4'b1111), .in14(4'b1111), .in15(4'b1111), .out(dstE), .sel(iCode));
  Multiplexer #(.select(4), .width(4)) multiplexer_2 (
    .in0(4'b1111), .in1(4'b1111), .in2(4'b1111), .in3(4'b1111), .in4(4'b1111), .in5(rA), .in6(4'b1111),
    .in7(4'b1111), .in8(4'b1111), .in9(4'b1111), .in10(4'b1111), .in11(rA), .in12(4'b1111), .in13(4'b1111),
    .in14(4'b1111), .in15(4'b1111), .out(dstM), .sel(iCode));
endmodule
